# Fritzing sketch Derby Car - Arduino Uno (saved by Fritzing 0.9.3b)
breadboards: 1

parts:
  Part1 = Arduino Uno (Rev3)
  Part2 = Adafruit LIS3DH [part_number="Adafruit #2809"]
  Part3 = NeoPixel Stick [part_number=1426]
  Part4 = NeoPixel Jewel [part_number=2226]
  Part5 = NeoPixel Stick [part_number=1426]

nets:
  N1: Part1.A4/SDA, Part2.SDA
  N2: Part1.A5/SCL, Part2.SCL
  N3: Part1.D5_PWM, Part3.DATAIN
  +5V: Part1.5V, Part2.VIN, Part3.+5V, Part4.VDD, Part5.+5V
  GND: Part1.GND, Part2.GND, Part3.GND, Part4.GND, Part5.GND
  N4: Part3.DATAOUT, Part5.DATAIN
  N5: Part4.IN, Part5.DATAOUT

custom parts:
  Adafruit LIS3DH: The LIS3DH is a very popular low power triple-axis accelerometer. It's low-cost, but has just about every 'extra' you'd want in an accelerometer: Three axis sensing, 10-bit precision ±2g/±4g/±8g/±16g selectable scaling Both I2C (2 possible addresses) and SPI interface options Interrupt output Multiple data rate options 1 Hz to 5Khz As low as 2uA current draw (just the chip itself, not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
  NeoPixel Stick: Make your own little LED strip arrangement with this stick of NeoPixel LEDs. We crammed 8 of the tiny 5050 (5mm x 5mm) smart RGB LEDs onto a PCB with mounting holes and a chainable design. Use only one microcontroller pin to control as many as you can chain together! Each LED is addressable as the driver chip is inside the LED. Each one has ~18mA constant current drive so the color will be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
  NeoPixel Jewel: We fit seven of our tiny 5050 (5mm x 5mm) smart RGB LEDs onto a beautiful, round PCB with mounting holes and a chainable design to create what we think is our most elegant (and evening-wear appropriate) NeoPixel board yet. Use only one microcontroller pin to control as many as you can chain together! Each LED is addressable as the driver chip is inside the LED. Each one has ~18mA constant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
