# Fritzing sketch Derby Car - Trinket (saved by Fritzing 0.9.3b)
breadboards: 1

parts:
  Part1 = Adafruit Trinket 3V [part_number="Adafruit #1500"]
  Part2 = Adafruit Switched JST Breakout [part_number="Adafruit #1863"]
  Part3 = Adafruit LIS3DH [part_number="Adafruit #2809"]
  U1 = LIPO-110mAh [package=lipo-110]  # not connected
  Part4 = NeoPixel Jewel [part_number=2226]
  Part5 = NeoPixel Stick [part_number=1426]
  Part6 = NeoPixel Stick [part_number=1426]

nets:
  +5V: Part1.VBAT, Part2.SW, Part3.VIN, Part4.VDD, Part5.+5V, Part6.+5V
  GND: Part1.GND, Part2.GND, Part3.GND, Part4.GND, Part5.GND, Part6.GND
  N1: Part1.#0, Part3.SDA
  N2: Part1.#1, Part3.SCL
  N3: Part1.#2, Part5.DATAIN
  N4: Part4.IN, Part6.DATAOUT
  N5: Part5.DATAOUT, Part6.DATAIN

custom parts:
  Adafruit Trinket 3V: Trinket may be small, but do not be fooled by its size! It's a tiny microcontroller board, built around the Atmel ATtiny85, a little chip with a lot of power. We wanted to design a microcontroller board that was small enough to fit into any project, and low cost enough to use without hesitation. Perfect for when you don't want to give up your expensive dev-board and you aren't willing to take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
  Adafruit Switched JST Breakout: This switched JST connector is the best way to quickly prototype with our LiPoly batteries. We paired a genuine JST connector with a slide switch that can do up to 600mA. Both are soldered onto a breadboard-friendly breakout. There's two ground pins, one 'switched' power pin, and one pin that is always on. This is compatible with the "JST PH 2-pin" connectors we use in our battery packs..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
  Adafruit LIS3DH: The LIS3DH is a very popular low power triple-axis accelerometer. It's low-cost, but has just about every 'extra' you'd want in an accelerometer: Three axis sensing, 10-bit precision ±2g/±4g/±8g/±16g selectable scaling Both I2C (2 possible addresses) and SPI interface options Interrupt output Multiple data rate options 1 Hz to 5Khz As low as 2uA current draw (just the chip itself, not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
  NeoPixel Jewel: We fit seven of our tiny 5050 (5mm x 5mm) smart RGB LEDs onto a beautiful, round PCB with mounting holes and a chainable design to create what we think is our most elegant (and evening-wear appropriate) NeoPixel board yet. Use only one microcontroller pin to control as many as you can chain together! Each LED is addressable as the driver chip is inside the LED. Each one has ~18mA constant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
  NeoPixel Stick: Make your own little LED strip arrangement with this stick of NeoPixel LEDs. We crammed 8 of the tiny 5050 (5mm x 5mm) smart RGB LEDs onto a PCB with mounting holes and a chainable design. Use only one microcontroller pin to control as many as you can chain together! Each LED is addressable as the driver chip is inside the LED. Each one has ~18mA constant current drive so the color will be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
